// Logisim project ex1.circ as structural Verilog: 6 circuits, main circuit main
module main (
);

  MyNAND mynand_1 ();  // open: in_1, in_2, out_3
endmodule

module MyNAND (
  input  in_1,
  input  in_2,
  output out_3
);

  wire and_1_out;

  and and_1 (and_1_out, in_1, in_2);
  not not_1 (out_3, and_1_out);
endmodule

module MyNOR (
  input  in_1,
  input  in_2,
  output out_3
);

  wire or_1_out;

  or or_1 (or_1_out, in_1, in_2);
  not not_1 (out_3, or_1_out);
endmodule

module MyXOR (
  input  in_1,
  input  in_2,
  output out_3
);

  wire and_1_out, and_2_out, not_1_out, not_2_out;

  not not_1 (not_1_out, in_1);
  and and_1 (and_1_out, not_1_out, in_2);
  and and_2 (and_2_out, in_1, not_2_out);
  not not_2 (not_2_out, in_2);
  or or_1 (out_3, and_1_out, and_2_out);
endmodule

module TMUX (
  input  in_1,
  input  in_2,
  input  in_3,
  output out_4
);

  wire and_1_out, and_2_out, not_1_out;

  not not_1 (not_1_out, in_2);
  and and_1 (and_1_out, not_1_out, in_1);
  and and_2 (and_2_out, in_2, in_3);
  or or_1 (out_4, and_1_out, and_2_out);
endmodule

module FMUX (
  input  in_1,
  input  in_2,
  input  in_3,
  input  in_4,
  input  in_5,
  input  in_6,
  output out_7
);

  wire tmux_1_out_4, tmux_2_out_4;

  TMUX tmux_1 (.in_1(in_1), .in_2(in_4), .in_3(in_2), .out_4(tmux_1_out_4));
  TMUX tmux_2 (.in_1(in_5), .in_2(in_4), .in_3(in_6), .out_4(tmux_2_out_4));
  TMUX tmux_3 (.in_1(tmux_1_out_4), .in_2(in_3), .in_3(tmux_2_out_4), .out_4(out_7));
endmodule
