// Logisim project ALU_starter.circ as structural Verilog: 10 circuits, main circuit main
module main (
  input  [31:0] IN1,
  input  [31:0] IN2,
  input  [2:0] Sel,
  output [31:0] OUT1
);

  // ALU alu_1: pin names not known; wires that end beside it: IN1, IN2, Sel, OUT1
endmodule

module ALU (
  input  [31:0] Input1,
  input  [2:0] Sel,
  input  [31:0] Input2,
  output [31:0] Output1
);

  wire [31:0] aand_1_out_3, exclusive_or_1_out_3, inclusive_or_1_out_3, rotate_left_1_out_3,
       rotate_right_1_out_3, shift_left_logical_1_out_3, shift_right_arthmetic_1_out_3,
       shift_right_logical_1_out_3;

  AAnd aand_1 (.In1(Input1), .In2(Input2), .out_3(aand_1_out_3));
  Shift_Left_Logical shift_left_logical_1 (.In1(Input1), .In2(Input2), .out_3(shift_left_logical_1_out_3));
  Rotate_left rotate_left_1 (.In1(Input1), .In2(Input2), .out_3(rotate_left_1_out_3));
  Rotate_Right rotate_right_1 (.In1(Input1), .In2(Input2), .out_3(rotate_right_1_out_3));
  Inclusive_Or inclusive_or_1 (.In1(Input1), .In2(Input2), .out_3(inclusive_or_1_out_3));
  Exclusive_Or exclusive_or_1 (.In1(Input1), .In2(Input2), .out_3(exclusive_or_1_out_3));
  Shift_Right_Logical shift_right_logical_1 (.In1(Input1), .In2(Input2), .out_3(shift_right_logical_1_out_3));
  Shift_Right_Arthmetic shift_right_arthmetic_1 (.In1(Input1), .In2(Input2), .out_3(shift_right_arthmetic_1_out_3));
  Multiplexer #(.select(3), .width(32), .enable("false")) multiplexer_1 (
    .in0(shift_left_logical_1_out_3), .in1(shift_right_logical_1_out_3), .in2(shift_right_arthmetic_1_out_3),
    .in3(rotate_left_1_out_3), .in4(rotate_right_1_out_3), .in5(aand_1_out_3), .in6(inclusive_or_1_out_3),
    .in7(exclusive_or_1_out_3), .out(Output1), .sel(Sel));
endmodule

module Shift_Left_Logical (
  input  [31:0] In1,
  input  [31:0] In2,
  output [31:0] out_3
);

  Shifter #(.width(32)) shifter_1 (.in(In1), .\dist (In2[4:0]), .out(out_3));
endmodule

module Shift_Right_Logical (
  input  [31:0] In1,
  input  [31:0] In2,
  output [31:0] out_3
);

  Shifter #(.width(32), .shift("lr")) shifter_1 (.in(In1), .\dist (In2[4:0]), .out(out_3));
endmodule

module Shift_Right_Arthmetic (
  input  [31:0] In1,
  input  [31:0] In2,
  output [31:0] out_3
);

  Shifter #(.width(32), .shift("ar")) shifter_1 (.in(In1), .\dist (In2[4:0]), .out(out_3));
endmodule

module Rotate_left (
  input  [31:0] In1,
  input  [31:0] In2,
  output [31:0] out_3
);

  Shifter #(.width(32), .shift("rl")) shifter_1 (.in(In1), .\dist (In2[4:0]), .out(out_3));
endmodule

module Rotate_Right (
  input  [31:0] In1,
  input  [31:0] In2,
  output [31:0] out_3
);

  Shifter #(.width(32), .shift("rr")) shifter_1 (.in(In1), .\dist (In2[4:0]), .out(out_3));
endmodule

module AAnd (
  input  [31:0] In1,
  input  [31:0] In2,
  output [31:0] out_3
);

  assign out_3 = In1 & In2;  // AND_Gate and_1, 32 bits wide
endmodule

module Inclusive_Or (
  input  [31:0] In1,
  input  [31:0] In2,
  output [31:0] out_3
);

  assign out_3 = In1 | In2;  // OR_Gate or_1, 32 bits wide
endmodule

module Exclusive_Or (
  input  [31:0] In1,
  input  [31:0] In2,
  output [31:0] out_3
);

  assign out_3 = In1 ^ In2;  // XOR_Gate xor_1, 32 bits wide
endmodule
