// Logisim project ex1.circ as structural Verilog: 3 circuits, main circuit main
module main (
  output Out1,
  output [7:0] Out2
);

  wire split_1_arm0, split_1_arm2;
  wire [5:0] split_1_arm1;

  Split split_1 (.in_1(8'h81), .Arm0(split_1_arm0), .Arm1(split_1_arm1), .Arm2(split_1_arm2));
  and and_1 (Out1, split_1_arm0, split_1_arm2);
  S_and_M s_and_m_1 (.D0(split_1_arm0), .D1_6(split_1_arm1), .D_7(split_1_arm2), .out_4(Out2));
endmodule

module Split (
  input  [7:0] in_1,
  output Arm0,
  output [5:0] Arm1,
  output Arm2
);


  assign Arm0 = in_1[0];
  assign Arm1 = in_1[6:1];
  assign Arm2 = in_1[7];
endmodule

module S_and_M (
  input  D0,
  input  [5:0] D1_6,
  input  D_7,
  output [7:0] out_4
);

  nor nor_1 (out_4[7], D0, 1'b1);

  assign out_4[6:0] = {D1_6, D_7};
endmodule
