// Logisim project ex2.circ as structural Verilog: 6 circuits, main circuit main
module main (
  output [15:0] out_1,
  output [15:0] out_2
);

  rotr rotr_1 (.B(4'b0101), .A(16'hb573), .out_3(out_1));

  assign out_2 = 16'hb573;
endmodule

module rotr (
  input  [3:0] B,
  input  [15:0] A,
  output [15:0] out_3
);

  wire decomposing_b_1_b0, decomposing_b_1_b1, decomposing_b_1_b2, decomposing_b_1_b3, decomposing_b_2_b0,
       decomposing_b_2_b1, decomposing_b_2_b2, decomposing_b_2_b3;
  wire [3:0] minusb_1_minusb;
  wire [15:0] sl_1_shift_l, sr_1_shift_r;

  MinusB minusb_1 (.B(B), .MinusB(minusb_1_minusb));
  decomposing_B decomposing_b_1 (
    .B(B), .B3(decomposing_b_1_b3), .B2(decomposing_b_1_b2), .B1(decomposing_b_1_b1), .B0(decomposing_b_1_b0));
  decomposing_B decomposing_b_2 (
    .B(minusb_1_minusb), .B3(decomposing_b_2_b3), .B2(decomposing_b_2_b2), .B1(decomposing_b_2_b1),
    .B0(decomposing_b_2_b0));
  SR sr_1 (
    .B3(decomposing_b_1_b3), .B2(decomposing_b_1_b2), .B1(decomposing_b_1_b1), .B0(decomposing_b_1_b0),
    .A(A), .Shift_R(sr_1_shift_r));
  SL sl_1 (
    .B3(decomposing_b_2_b3), .B2(decomposing_b_2_b2), .B1(decomposing_b_2_b1), .B0(decomposing_b_2_b0),
    .A(A), .Shift_L(sl_1_shift_l));
  assign out_3 = sr_1_shift_r | sl_1_shift_l;  // OR_Gate or_1, 16 bits wide
endmodule

module decomposing_B (
  input  [3:0] B,
  output B3,
  output B2,
  output B1,
  output B0
);


  assign B0 = B[0];
  assign B1 = B[1];
  assign B2 = B[2];
  assign B3 = B[3];
endmodule

module SR (
  input  B3,
  input  B2,
  input  B1,
  input  B0,
  input  [15:0] A,
  output [15:0] Shift_R
);

  wire [15:0] multiplexer_1_out, multiplexer_2_out, multiplexer_3_out;

  Multiplexer #(.width(16), .enable("false")) multiplexer_1 (
    .in0(A), .in1({{8{1'b0}}, A[15:8]}), .out(multiplexer_1_out), .sel(B3));
  Multiplexer #(.width(16), .enable("false")) multiplexer_2 (
    .in0(multiplexer_1_out), .in1({4'b0000, multiplexer_1_out[15:4]}), .out(multiplexer_2_out), .sel(B2));
  Multiplexer #(.width(16), .enable("false")) multiplexer_3 (
    .in0(multiplexer_2_out), .in1({2'b00, multiplexer_2_out[15:2]}), .out(multiplexer_3_out), .sel(B1));
  Multiplexer #(.width(16), .enable("false")) multiplexer_4 (
    .in0(multiplexer_3_out), .in1({1'b0, multiplexer_3_out[15:1]}), .out(Shift_R), .sel(B0));
endmodule

module SL (
  input  B3,
  input  B2,
  input  B1,
  input  B0,
  input  [15:0] A,
  output [15:0] Shift_L
);

  wire [15:0] multiplexer_1_out, multiplexer_2_out, multiplexer_3_out;

  Multiplexer #(.width(16), .enable("false")) multiplexer_1 (
    .in0(A), .in1({A[7:0], {8{1'b0}}}), .out(multiplexer_1_out), .sel(B3));
  Multiplexer #(.width(16), .enable("false")) multiplexer_2 (
    .in0(multiplexer_1_out), .in1({multiplexer_1_out[11:0], 4'b0000}), .out(multiplexer_2_out), .sel(B2));
  Multiplexer #(.width(16), .enable("false")) multiplexer_3 (
    .in0(multiplexer_2_out), .in1({multiplexer_2_out[13:0], 2'b00}), .out(multiplexer_3_out), .sel(B1));
  Multiplexer #(.width(16), .enable("false")) multiplexer_4 (
    .in0(multiplexer_3_out), .in1({multiplexer_3_out[14:0], 1'b0}), .out(Shift_L), .sel(B0));
endmodule

module MinusB (
  input  [3:0] B,
  output [3:0] MinusB
);

  wire [4:4] subtractor_1_out;

  Subtractor #(.width(5)) subtractor_1 (
    .a(5'b10000), .b({1'b0, B}), .out({subtractor_1_out[4], MinusB}));  // open: bin, bout
endmodule
