// Logisim project ex1.circ as structural Verilog: 2 circuits, main circuit main
module main (
  input  [4:0] in_1,
  output [9:0] out_2
);

  wire button_1_out, clock_1_out, count_1_out_4;
  wire [9:0] adder_1_out, register_1_q;

  Adder #(.width(10)) adder_1 (.a(out_2), .b(register_1_q), .out(adder_1_out));  // open: cin, cout
  Clock clock_1 (.out(clock_1_out));
  Button button_1 (.out(button_1_out));
  Register #(.width(10)) register_1 (
    .D(adder_1_out), .en(count_1_out_4), .clk(clock_1_out), .Q(register_1_q));  // open: clr
  Register #(.width(10)) register_2 (.D(register_1_q), .en(count_1_out_4), .clk(clock_1_out), .Q(out_2));  // open: clr
  count count_1 (.Reset(button_1_out), .Count(clock_1_out), .in_3(in_1), .out_4(count_1_out_4));
endmodule

module count (
  input  Reset,
  input  Count,
  input  [4:0] in_3,
  output out_4
);

  wire [4:0] counter_1_q;

  Counter #(.width(5), .max('h1f)) counter_1 (
    .clr(Reset), .count(out_4), .clk(Count), .Q(counter_1_q));  // open: load, up, D, carry
  // Probe on counter_1_q
  Comparator #(.width(5), .mode("unsigned")) comparator_1 (.a(counter_1_q), .b(in_3), .lt(out_4));  // open: gt, eq
endmodule
