// Logisim project alu.circ as structural Verilog: 2 circuits, main circuit alu
module alu (
  input  [31:0] A,
  input  [31:0] B,
  input  [3:0] ALUSel,
  output [31:0] Result,
  output [31:0] out_5
);

  wire comparator_1_lt;
  wire [6:0] bitadder_1_out;
  wire [31:0] add, alu_and, alu_cnto, alu_divu, alu_mulh, alu_mulhu, alu_mult, alu_or, alu_remu, alu_sll,
       alu_slt, alu_sra, alu_srl, alu_sub, alu_xor;

  Multiplexer #(.select(4), .width(32), .enable("false")) multiplexer_1 (
    .in0(add), .in1(alu_and), .in2(alu_or), .in3(alu_xor), .in4(alu_srl), .in5(alu_sra), .in6(alu_sll),
    .in7(alu_slt), .in8(alu_divu), .in9(alu_remu), .in10(alu_mult), .in11(alu_mulhu), .in12(alu_sub),
    .in13(alu_cnto), .in14(alu_mulh), .out(Result), .sel(ALUSel));  // open: in15
  Adder #(.width(32)) adder_1 (.a(A), .b(B), .out(add));  // open: cin, cout
  assign alu_and = A & B;  // AND_Gate and_1, 32 bits wide
  assign alu_or = A | B;  // OR_Gate or_1, 32 bits wide
  assign alu_xor = A ^ B;  // XOR_Gate xor_1, 32 bits wide
  Shifter #(.width(32), .shift("lr")) shifter_1 (.in(A), .\dist (B[4:0]), .out(alu_srl));
  Shifter #(.width(32), .shift("ar")) shifter_2 (.in(A), .\dist (B[4:0]), .out(alu_sra));
  Shifter #(.width(32)) shifter_3 (.in(A), .\dist (B[4:0]), .out(alu_sll));
  Comparator #(.width(32)) comparator_1 (.a(A), .b(B), .lt(comparator_1_lt));  // open: gt, eq
  Divider #(.width(32)) divider_1 (.a(A), .b(B), .out(alu_divu), .rem(alu_remu));  // open: upper
  Multiplier #(.width(32)) multiplier_1 (.a(A), .b(B), .out(alu_mult), .cout(alu_mulhu));  // open: cin
  Subtractor #(.width(32)) subtractor_1 (.a(A), .b(B), .out(alu_sub));  // open: bin, bout
  BitAdder #(.width(32)) bitadder_1 (.in0(A), .in1(B), .out(bitadder_1_out));
  mulh mulh_1 (.in_1(A), .in_2(B), .out_3(alu_mulh));
  assign alu_slt = {{31{1'b0}}, comparator_1_lt};  // Bit_Extender bit_extender_1
  assign alu_cnto = {{25{1'b0}}, bitadder_1_out};  // Bit_Extender bit_extender_2

  // Notes on the sheet:
  //   INPUTS to your circuit
  //   DON'T CHANGE THE LOCATIONS OF THE INPUTS AND OUTPUTS!
  //   OUTPUT from your circuit
endmodule

module mulh (
  input  [31:0] in_1,
  input  [31:0] in_2,
  output [31:0] out_3
);

  wire AddOne_Sel, xor_1_out;
  wire [31:0] adder_1_out, multiplexer_1_out, multiplexer_2_out, multiplexer_3_out, multiplier_1_cout,
       multiplier_1_out, negator_1_out, negator_2_out, not_1_out;

  Negator #(.width(32)) negator_1 (.in(in_1), .out(negator_1_out));
  Negator #(.width(32)) negator_2 (.in(in_2), .out(negator_2_out));
  Multiplexer #(.width(32), .enable("false")) multiplexer_1 (
    .in0(in_1), .in1(negator_1_out), .out(multiplexer_1_out), .sel(in_1[31]));
  Multiplexer #(.width(32), .enable("false")) multiplexer_2 (
    .in0(in_2), .in1(negator_2_out), .out(multiplexer_2_out), .sel(in_2[31]));
  Multiplier #(.width(32)) multiplier_1 (
    .a(multiplexer_1_out), .b(multiplexer_2_out), .out(multiplier_1_out), .cout(multiplier_1_cout));  // open: cin
  assign not_1_out = ~multiplier_1_cout;  // NOT_Gate not_1, 32 bits wide
  Multiplexer #(.width(32), .enable("false")) multiplexer_3 (
    .in0(multiplier_1_cout), .in1(not_1_out), .out(multiplexer_3_out), .sel(xor_1_out));
  xor xor_1 (xor_1_out, in_1[31], in_2[31]);
  Comparator #(.width(32)) comparator_1 (.a(multiplier_1_out), .b({32{1'b0}}), .eq(AddOne_Sel));  // open: gt, lt
  Adder #(.width(32)) adder_1 (.a(multiplexer_3_out), .b(32'h1), .out(adder_1_out));  // open: cin, cout
  Multiplexer #(.width(32), .enable("false")) multiplexer_4 (
    .in0(multiplexer_3_out), .in1(adder_1_out), .out(out_3), .sel(AddOne_Sel));

  // Other names for the same wires on the sheet: Neg_SelA = in_1[31]; Neg_SelB = in_2[31]
endmodule
