// Logisim project regfile.circ as structural Verilog: 2 circuits, main circuit main
module main (
  input  [4:0] rs1,
  input  [4:0] rs2,
  input  [4:0] rd,
  input  [31:0] Write_Data,
  input  RegWEn,
  input  clk,
  output [31:0] ra,
  output [31:0] sp,
  output [31:0] t0,
  output [31:0] t1,
  output [31:0] t2,
  output [31:0] s0,
  output [31:0] s1,
  output [31:0] a0,
  output [31:0] Read_Data_1,
  output [31:0] Read_Data_2
);

  wire [31:0] reglogic_1_regx0;

  RegLogic reglogic_1 (
    .WriteData(Write_Data), .clk(clk), .WriteReg(rd), .readreg1(rs1), .readreg2(rs2), .RegWEn(RegWEn),
    .regx0(reglogic_1_regx0), .regx1(ra), .regx2(sp), .regx5(t0), .regx6(t1), .regx7(t2), .regx8(s0),
    .regx9(s1), .regx10(a0), .reg1data(Read_Data_1), .reg2data(Read_Data_2));

  // Other names for the same wires on the sheet: read_data1[31:0] = Read_Data_1; read_data2[31:0] = Read_Data_2;
  //   read_reg1[4:0] = rs1; read_reg2[4:0] = rs2; write_en = RegWEn; write_reg[4:0] = rd

  // Notes on the sheet:
  //   INPUTS to your circuit
  //   DON'T CHANGE THE LOCATIONS OF THE INPUTS AND OUTPUTS!
  //   These are DEBUG/TEST outputs from your circuit.
  //   OUTPUTS from your circuit
endmodule

module RegLogic (
  input  [31:0] WriteData,
  input  clk,
  input  [4:0] WriteReg,
  input  [4:0] readreg1,
  input  [4:0] readreg2,
  input  RegWEn,
  output [31:0] regx0,
  output [31:0] regx1,
  output [31:0] regx2,
  output [31:0] regx5,
  output [31:0] regx6,
  output [31:0] regx7,
  output [31:0] regx8,
  output [31:0] regx9,
  output [31:0] regx10,
  output [31:0] reg1data,
  output [31:0] reg2data
);

  wire demultiplexer_1_out1, demultiplexer_1_out2, demultiplexer_1_out5, demultiplexer_1_out6,
       demultiplexer_1_out7, demultiplexer_1_out8, demultiplexer_1_out9, demultiplexer_1_out10;
  wire [31:0] demultiplexer_2_out1, demultiplexer_2_out2, demultiplexer_2_out5, demultiplexer_2_out6,
       demultiplexer_2_out7, demultiplexer_2_out8, demultiplexer_2_out9, demultiplexer_2_out10;

  Demultiplexer #(.select(5), .enable("false")) demultiplexer_1 (
    .out1(demultiplexer_1_out1), .out2(demultiplexer_1_out2), .out5(demultiplexer_1_out5),
    .out6(demultiplexer_1_out6), .out7(demultiplexer_1_out7), .out8(demultiplexer_1_out8),
    .out9(demultiplexer_1_out9), .out10(demultiplexer_1_out10), .in(RegWEn), .sel(WriteReg));  // open: out0, out3, out4, out11, out12, out13, out14, out15, out16, out17, out18, out19, out20, out21, out22, out23, out24, out25, out26, out27, out28, out29, out30, out31
  Demultiplexer #(.select(5), .width(32), .enable("false")) demultiplexer_2 (
    .out1(demultiplexer_2_out1), .out2(demultiplexer_2_out2), .out5(demultiplexer_2_out5),
    .out6(demultiplexer_2_out6), .out7(demultiplexer_2_out7), .out8(demultiplexer_2_out8),
    .out9(demultiplexer_2_out9), .out10(demultiplexer_2_out10), .in(WriteData), .sel(WriteReg));  // open: out0, out3, out4, out11, out12, out13, out14, out15, out16, out17, out18, out19, out20, out21, out22, out23, out24, out25, out26, out27, out28, out29, out30, out31
  Register #(.width(32)) x0 (.D({32{1'b0}}), .en(1'b1), .clk(clk), .Q(regx0));  // open: clr
  Register #(.width(32)) x1 (.D(demultiplexer_2_out1), .en(demultiplexer_1_out1), .clk(clk), .Q(regx1));  // open: clr
  Register #(.width(32)) x2 (.D(demultiplexer_2_out2), .en(demultiplexer_1_out2), .clk(clk), .Q(regx2));  // open: clr
  Register #(.width(32)) x5 (.D(demultiplexer_2_out5), .en(demultiplexer_1_out5), .clk(clk), .Q(regx5));  // open: clr
  Register #(.width(32)) x6 (.D(demultiplexer_2_out6), .en(demultiplexer_1_out6), .clk(clk), .Q(regx6));  // open: clr
  Register #(.width(32)) x7 (.D(demultiplexer_2_out7), .en(demultiplexer_1_out7), .clk(clk), .Q(regx7));  // open: clr
  Register #(.width(32)) x8 (.D(demultiplexer_2_out8), .en(demultiplexer_1_out8), .clk(clk), .Q(regx8));  // open: clr
  Register #(.width(32)) x9 (.D(demultiplexer_2_out9), .en(demultiplexer_1_out9), .clk(clk), .Q(regx9));  // open: clr
  Register #(.width(32)) x10 (
    .D(demultiplexer_2_out10), .en(demultiplexer_1_out10), .clk(clk), .Q(regx10));  // open: clr
  Multiplexer #(.select(5), .width(32), .enable("false")) multiplexer_1 (
    .in0(regx0), .in1(regx1), .in2(regx2), .in5(regx5), .in6(regx6), .in7(regx7), .in8(regx8), .in9(regx9),
    .in10(regx10), .out(reg1data), .sel(readreg1));  // open: in3, in4, in11, in12, in13, in14, in15, in16, in17, in18, in19, in20, in21, in22, in23, in24, in25, in26, in27, in28, in29, in30, in31
  Multiplexer #(.select(5), .width(32), .enable("false")) multiplexer_2 (
    .in0(regx0), .in1(regx1), .in2(regx2), .in5(regx5), .in6(regx6), .in7(regx7), .in8(regx8), .in9(regx9),
    .in10(regx10), .out(reg2data), .sel(readreg2));  // open: in3, in4, in11, in12, in13, in14, in15, in16, in17, in18, in19, in20, in21, in22, in23, in24, in25, in26, in27, in28, in29, in30, in31
endmodule
