// Logisim project cpu.circ as structural Verilog: 4 circuits, main circuit main
module main (
  input  [31:0] INSTRUCTION,
  input  CLOCK,
  output [31:0] FETCH_ADDRESS,
  output [31:0] ra,
  output [31:0] sp,
  output [31:0] t0,
  output [31:0] t1,
  output [31:0] t2,
  output [31:0] s0,
  output [31:0] s1,
  output [31:0] a0
);

  wire iBrEq, iBrLT, oAsel, oBrUn, oBsel, oMemRW, oPCSel, oRegWEn;
  wire [1:0] oWBSel;
  wire [2:0] oImmSel;
  wire [3:0] oALUSel;
  wire [31:0] adder_1_out, adder_2_out, Arithmetic_Logic_Unit_result, divider_1_out, DMEM_p5, immgen_1_imme,
       Instruction_t, multiplexer_1_out, multiplexer_2_out, multiplexer_3_out, multiplexer_4_out,
       multiplexer_5_out, multiplier_1_out, RegFile_read_data_1, RegFile_read_data_2, register_1_q;

  Adder #(.width(32)) adder_1 (.a(FETCH_ADDRESS), .b(32'h1), .out(adder_1_out));  // open: cin, cout
  Register #(.width(32)) PC (.D(multiplexer_1_out), .clk(CLOCK), .Q(FETCH_ADDRESS));  // open: en, clr
  Multiplexer #(.width(32), .enable("false")) multiplexer_1 (
    .in0(adder_1_out), .in1(divider_1_out), .out(multiplexer_1_out), .sel(oPCSel));
  Divider #(.width(32)) divider_1 (
    .a(Arithmetic_Logic_Unit_result), .b(32'h4), .out(divider_1_out));  // open: upper, rem
  Control control_1 (
    .Instruction(Instruction_t), .BrEq(iBrEq), .BrLT(iBrLT), .PCSel(oPCSel), .ImmSel(oImmSel), .BrUn(oBrUn),
    .ASel(oAsel), .Bsel(oBsel), .ALUSel(oALUSel), .MemRW(oMemRW), .RegWEn(oRegWEn), .WBSel(oWBSel));
  Register #(.width(32)) register_1 (.D(FETCH_ADDRESS), .clk(CLOCK), .Q(register_1_q));  // open: en, clr
  Multiplexer #(.width(32), .enable("false")) multiplexer_2 (
    .in0(INSTRUCTION), .in1(32'h13), .out(multiplexer_2_out), .sel(oPCSel));
  Adder #(.width(32)) adder_2 (.a(register_1_q), .b(32'h4), .out(adder_2_out));  // open: cin, cout
  Register #(.width(32)) register_2 (.D(multiplexer_2_out), .clk(CLOCK), .Q(Instruction_t));  // open: en, clr
  ImmGen immgen_1 (.Inst(Instruction_t[31:7]), .ImmSel(oImmSel), .Imme(immgen_1_imme));
  regfile_main RegFile (
    .rs2(Instruction_t[24:20]), .rd(Instruction_t[11:7]), .Read_Data_1(RegFile_read_data_1),
    .Read_Data_2(RegFile_read_data_2), .ra(ra), .sp(sp), .t0(t0), .t1(t1), .t2(t2), .s0(s0), .s1(s1),
    .a0(a0), .rs1(Instruction_t[19:15]), .Write_Data(multiplexer_5_out), .RegWEn(oRegWEn), .clk(CLOCK));
  Multiplier #(.width(32)) multiplier_1 (.a(register_1_q), .b(32'h4), .out(multiplier_1_out));  // open: cin, cout
  BranchComp branchcomp_1 (.A(RegFile_read_data_1), .B(RegFile_read_data_2), .BrUn(oBrUn), .BrEq(iBrEq), .BrLT(iBrLT));
  Multiplexer #(.width(32), .enable("false")) multiplexer_3 (
    .in0(RegFile_read_data_1), .in1(multiplier_1_out), .out(multiplexer_3_out), .sel(oAsel));
  Multiplexer #(.width(32), .enable("false")) multiplexer_4 (
    .in0(RegFile_read_data_2), .in1(immgen_1_imme), .out(multiplexer_4_out), .sel(oBsel));
  alu Arithmetic_Logic_Unit (
    .A(multiplexer_3_out), .B(multiplexer_4_out), .ALUSel(oALUSel), .Result(Arithmetic_Logic_Unit_result));  // open: out_5
  // mem_main DMEM: pin names not known; wires that end beside it: Arithmetic_Logic_Unit_result, RegFile_read_data_2, oMemRW, CLOCK, DMEM_p5
  Multiplexer #(.select(2), .width(32), .enable("false")) multiplexer_5 (
    .in0(DMEM_p5), .in1(Arithmetic_Logic_Unit_result), .in2(adder_2_out), .out(multiplexer_5_out),
    .sel(oWBSel));  // open: in3

  // Other names for the same wires on the sheet: clk = CLOCK; fetch_addr[31:0] = FETCH_ADDRESS

  // Notes on the sheet:
  //   Output
  //   Inputs/Outputs from run.circ. DO NOT MOVE THESE.
  //   Inputs
  //   Inputs/Outputs from run.circ. DO NOT MOVE THESE.
endmodule

module ImmGen (
  input  [24:0] Inst,
  input  [2:0] ImmSel,
  output [31:0] Imme
);

  wire [31:0] B, I, J, S;

  assign I = {{20{Inst[24]}}, Inst[24:13]};  // Bit_Extender bit_extender_1
  assign S = {{20{Inst[24]}}, {Inst[24:18], Inst[4:0]}};  // Bit_Extender bit_extender_2
  assign B = {{19{Inst[24]}}, {Inst[24], Inst[0], Inst[23:18], Inst[4:1], 1'b0}};  // Bit_Extender bit_extender_3
  assign J = {{11{Inst[24]}}, {Inst[24], Inst[12:5], Inst[13], Inst[23:14], 1'b0}};  // Bit_Extender bit_extender_4
  Multiplexer #(.select(3), .width(32), .enable("false")) multiplexer_1 (
    .in0(I), .in1(S), .in2(B), .in3({Inst[24:5], {12{1'b0}}}), .in4(J), .out(Imme), .sel(ImmSel));  // open: in5, in6, in7

  // Other names for the same wires on the sheet: B811[3:0] = Inst[4:1]; B7 = Inst[0]; B2124[3:0] = Inst[17:14];
  //   U[31:12] = Inst[24:5]; B2530[5:0] = Inst[23:18]; B20 = Inst[13]; B1219[7:0] = Inst[12:5]; B31 = Inst[24]

  // Notes on the sheet:
  //   7;8-11;12-19;20;21-24;25-30;31
  //   000 I  001 S  010 B  011 U  100 J
endmodule

module BranchComp (
  input  [31:0] A,
  input  [31:0] B,
  input  BrUn,
  output BrEq,
  output BrLT
);

  wire comparator_1_eq, comparator_1_lt, comparator_2_eq, comparator_2_lt;

  Comparator #(.width(32)) comparator_1 (.a(A), .b(B), .eq(comparator_1_eq), .lt(comparator_1_lt));  // open: gt
  Comparator #(.width(32), .mode("unsigned")) comparator_2 (
    .a(A), .b(B), .eq(comparator_2_eq), .lt(comparator_2_lt));  // open: gt
  Multiplexer #(.enable("false")) multiplexer_1 (.in0(comparator_1_eq), .in1(comparator_2_eq), .out(BrEq), .sel(BrUn));
  Multiplexer #(.enable("false")) multiplexer_2 (.in0(comparator_1_lt), .in1(comparator_2_lt), .out(BrLT), .sel(BrUn));
endmodule

module Control (
  input  [31:0] Instruction,
  input  BrEq,
  input  BrLT,
  output PCSel,
  output [2:0] ImmSel,
  output BrUn,
  output ASel,
  output Bsel,
  output [3:0] ALUSel,
  output MemRW,
  output RegWEn,
  output [1:0] WBSel
);

  wire and_1_out, and_2_out, and_3_out, and_4_out, comparator_1_eq, comparator_2_eq, comparator_3_eq,
       comparator_4_eq, comparator_5_eq, comparator_6_eq, comparator_7_eq, comparator_8_eq, comparator_9_eq,
       comparator_10_eq, comparator_11_eq, comparator_12_eq, comparator_13_eq, comparator_14_eq,
       comparator_15_eq, comparator_16_eq, comparator_17_eq, multiplexer_4_out, not_1_out, or_1_out,
       or_2_out, or_3_out, PCSel_t;
  wire [0:0] rom_1_data;
  wire [1:0] adder_8_out, adder_9_out, Addr67, bit_extender_9_out, bit_extender_10_out, bit_extender_11_out,
       multiplexer_2_out, multiplier_9_out, multiplier_10_out, multiplier_11_out;
  wire [2:0] adder_1_out, adder_2_out, adder_3_out, adder_4_out, adder_5_out, adder_6_out, Addr02,
       bit_extender_1_out, bit_extender_2_out, bit_extender_3_out, bit_extender_4_out, bit_extender_5_out,
       bit_extender_6_out, bit_extender_7_out, bit_extender_8_out, multiplier_1_out, multiplier_2_out,
       multiplier_3_out, multiplier_4_out, multiplier_5_out, multiplier_6_out, multiplier_7_out,
       multiplier_8_out;
  wire [7:0] multiplexer_1_out;

  Comparator #(.width(7), .mode("unsigned")) comparator_1 (
    .a(Instruction[6:0]), .b(7'b0110011), .eq(comparator_1_eq));  // open: gt, lt
  Comparator #(.width(7), .mode("unsigned")) comparator_2 (
    .a(Instruction[6:0]), .b(7'b0000011), .eq(comparator_2_eq));  // open: gt, lt
  Comparator #(.width(7), .mode("unsigned")) comparator_3 (
    .a(Instruction[6:0]), .b(7'b0010011), .eq(comparator_3_eq));  // open: gt, lt
  Comparator #(.width(7), .mode("unsigned")) comparator_4 (
    .a(Instruction[6:0]), .b(7'b0100011), .eq(comparator_4_eq));  // open: gt, lt
  Comparator #(.width(7), .mode("unsigned")) comparator_5 (
    .a(Instruction[6:0]), .b(7'b1100011), .eq(comparator_5_eq));  // open: gt, lt
  Comparator #(.width(7), .mode("unsigned")) comparator_6 (
    .a(Instruction[6:0]), .b(7'b0110111), .eq(comparator_6_eq));  // open: gt, lt
  Comparator #(.width(7), .mode("unsigned")) comparator_7 (
    .a(Instruction[6:0]), .b(7'b1101111), .eq(comparator_7_eq));  // open: gt, lt
  Comparator #(.width(7), .mode("unsigned")) comparator_8 (
    .a(Instruction[6:0]), .b(7'b1100111), .eq(comparator_8_eq));  // open: gt, lt
  assign bit_extender_1_out = {{2{1'b0}}, comparator_1_eq};  // Bit_Extender bit_extender_1
  assign bit_extender_2_out = {{2{1'b0}}, comparator_2_eq};  // Bit_Extender bit_extender_2
  assign bit_extender_3_out = {{2{1'b0}}, comparator_3_eq};  // Bit_Extender bit_extender_3
  assign bit_extender_4_out = {{2{1'b0}}, comparator_4_eq};  // Bit_Extender bit_extender_4
  assign bit_extender_5_out = {{2{1'b0}}, comparator_5_eq};  // Bit_Extender bit_extender_5
  assign bit_extender_6_out = {{2{1'b0}}, comparator_6_eq};  // Bit_Extender bit_extender_6
  assign bit_extender_7_out = {{2{1'b0}}, comparator_7_eq};  // Bit_Extender bit_extender_7
  assign bit_extender_8_out = {{2{1'b0}}, comparator_8_eq};  // Bit_Extender bit_extender_8
  Multiplier #(.width(3)) multiplier_1 (.a(3'b000), .b(bit_extender_1_out), .out(multiplier_1_out));  // open: cin, cout
  Adder #(.width(3)) adder_1 (.a(multiplier_1_out), .b(multiplier_2_out), .out(adder_1_out));  // open: cin, cout
  Multiplier #(.width(3)) multiplier_2 (.a(3'b001), .b(bit_extender_2_out), .out(multiplier_2_out));  // open: cin, cout
  Multiplier #(.width(3)) multiplier_3 (.a(3'b010), .b(bit_extender_3_out), .out(multiplier_3_out));  // open: cin, cout
  Adder #(.width(3)) adder_2 (.a(multiplier_3_out), .b(multiplier_4_out), .out(adder_2_out));  // open: cin, cout
  Multiplier #(.width(3)) multiplier_4 (.a(3'b011), .b(bit_extender_4_out), .out(multiplier_4_out));  // open: cin, cout
  Multiplier #(.width(3)) multiplier_5 (.a(3'b100), .b(bit_extender_5_out), .out(multiplier_5_out));  // open: cin, cout
  Adder #(.width(3)) adder_3 (.a(multiplier_5_out), .b(multiplier_6_out), .out(adder_3_out));  // open: cin, cout
  Multiplier #(.width(3)) multiplier_6 (.a(3'b101), .b(bit_extender_6_out), .out(multiplier_6_out));  // open: cin, cout
  Multiplier #(.width(3)) multiplier_7 (.a(3'b110), .b(bit_extender_7_out), .out(multiplier_7_out));  // open: cin, cout
  Adder #(.width(3)) adder_4 (.a(multiplier_7_out), .b(multiplier_8_out), .out(adder_4_out));  // open: cin, cout
  Multiplier #(.width(3)) multiplier_8 (.a(3'b111), .b(bit_extender_8_out), .out(multiplier_8_out));  // open: cin, cout
  Adder #(.width(3)) adder_5 (.a(adder_1_out), .b(adder_2_out), .out(adder_5_out));  // open: cin, cout
  Adder #(.width(3)) adder_6 (.a(adder_3_out), .b(adder_4_out), .out(adder_6_out));  // open: cin, cout
  ROM #(.dataWidth(16)) rom_1 (
    .addr(multiplexer_1_out),
    .data({PCSel_t, ImmSel, BrUn, ASel, Bsel, ALUSel, MemRW, RegWEn, WBSel, rom_1_data[0]}));
  Multiplexer #(.select(3), .width(8), .enable("false")) multiplexer_1 (
    .in0({Addr02, Instruction[14:12], Addr67}), .in1({Addr02, Instruction[14:12], 2'b00}),
    .in2({Addr02, Instruction[14:12], Addr67}), .in3({Addr02, {5{1'b0}}}),
    .in4({Addr02, Instruction[14:12], 2'b00}), .in5({Addr02, {5{1'b0}}}), .in6({Addr02, {5{1'b0}}}),
    .in7({Addr02, {5{1'b0}}}), .out(multiplexer_1_out), .sel(Addr02));
  Adder #(.width(3)) adder_7 (.a(adder_5_out), .b(adder_6_out), .out(Addr02));  // open: cin, cout
  Comparator #(.width(7), .mode("unsigned")) comparator_9 (
    .a(Instruction[31:25]), .b({7{1'b0}}), .eq(comparator_9_eq));  // open: gt, lt
  Comparator #(.width(7), .mode("unsigned")) comparator_10 (
    .a(Instruction[31:25]), .b(7'b0000001), .eq(comparator_10_eq));  // open: gt, lt
  Comparator #(.width(7), .mode("unsigned")) comparator_11 (
    .a(Instruction[31:25]), .b(7'b0100000), .eq(comparator_11_eq));  // open: gt, lt
  assign bit_extender_9_out = {{1{1'b0}}, comparator_9_eq};  // Bit_Extender bit_extender_9
  assign bit_extender_10_out = {{1{1'b0}}, comparator_10_eq};  // Bit_Extender bit_extender_10
  assign bit_extender_11_out = {{1{1'b0}}, comparator_11_eq};  // Bit_Extender bit_extender_11
  Multiplier #(.width(2)) multiplier_9 (.a(2'b01), .b(bit_extender_9_out), .out(multiplier_9_out));  // open: cin, cout
  Multiplier #(.width(2)) multiplier_10 (
    .a(2'b10), .b(bit_extender_10_out), .out(multiplier_10_out));  // open: cin, cout
  Multiplier #(.width(2)) multiplier_11 (
    .a(2'b11), .b(bit_extender_11_out), .out(multiplier_11_out));  // open: cin, cout
  Adder #(.width(2)) adder_8 (.a(multiplier_9_out), .b(multiplier_10_out), .out(adder_8_out));  // open: cin, cout
  Adder #(.width(2)) adder_9 (.a(adder_8_out), .b(multiplier_11_out), .out(adder_9_out));  // open: cin, cout
  Comparator #(.width(3), .mode("unsigned")) comparator_12 (
    .a(Instruction[14:12]), .b(3'b000), .eq(comparator_12_eq));  // open: gt, lt
  Comparator #(.width(3), .mode("unsigned")) comparator_13 (
    .a(Instruction[14:12]), .b(3'b100), .eq(comparator_13_eq));  // open: gt, lt
  Comparator #(.width(3), .mode("unsigned")) comparator_14 (
    .a(Instruction[14:12]), .b(3'b110), .eq(comparator_14_eq));  // open: gt, lt
  Comparator #(.width(3), .mode("unsigned")) comparator_15 (
    .a(Instruction[14:12]), .b(3'b000), .eq(comparator_15_eq));  // open: gt, lt
  not not_1 (not_1_out, BrEq);
  Multiplexer #(.select(3), .width(2), .enable("false")) multiplexer_2 (
    .in0(2'b00), .in1(adder_9_out), .in2(2'b00), .in3(2'b00), .in4(2'b00), .in5(adder_9_out), .in6(2'b00),
    .in7(2'b00), .out(multiplexer_2_out), .sel(Instruction[14:12]));
  and and_1 (and_1_out, comparator_12_eq, BrEq);
  and and_2 (and_2_out, comparator_13_eq, BrLT);
  and and_3 (and_3_out, comparator_14_eq, BrLT);
  and and_4 (and_4_out, comparator_15_eq, not_1_out);
  or or_1 (or_1_out, and_1_out, and_2_out);
  or or_2 (or_2_out, or_1_out, or_3_out);
  or or_3 (or_3_out, and_3_out, and_4_out);
  Multiplexer #(.width(2), .enable("false")) multiplexer_3 (
    .in0(adder_9_out), .in1(multiplexer_2_out), .out(Addr67), .sel(comparator_16_eq));
  Comparator #(.width(3)) comparator_16 (.a(Addr02), .b(3'b010), .eq(comparator_16_eq));  // open: gt, lt
  Multiplexer #(.enable("false")) multiplexer_4 (.in0(1'b0), .in1(1'b1), .out(multiplexer_4_out), .sel(or_2_out));
  Comparator #(.width(3), .mode("unsigned")) comparator_17 (
    .a(Addr02), .b(3'b100), .eq(comparator_17_eq));  // open: gt, lt
  Multiplexer #(.enable("false")) multiplexer_5 (
    .in0(PCSel_t), .in1(multiplexer_4_out), .out(PCSel), .sel(comparator_17_eq));

  // Other names for the same wires on the sheet: Addr35[2:0] = Instruction[14:12]; funct3[2:0] = Instruction[14:12];
  //   opcode[6:0] = Instruction[6:0]; funct7[6:0] = Instruction[31:25]

  // Notes on the sheet:
  //   opcode has 8 different types
  //   Sel1:select by opcode in to 8 differentcatagories
  //   contents of rom_1 (hex, n*v repeats v):
  //   0 a 14a 18a 0 ca 1ca 0 0 ea 4*0 16a 0 0 6a 0 0 0 8a 20a 0 0 4a 0 0 0 2a 12a 0 208 0 0 0 208 0 0 0
  //   208 23*0 20a 4*0 2ca 0 0 2ea 7*0 26a 4*0 28a 0 2aa 24a 0 0 0 20a 0 0 0 1210 31*0 2600 0 0 0 2600
  //   11*0 a600 7*0 ae00 7*0 33ea 31*0 c60c 31*0 820c
  //   function 3 uses itself
  //   00:01; 01:02; 20:03; else:00
endmodule
